# Fritzing sketch DoorSign (saved by Fritzing 0.9.3b)
circuit board: 8.46667cm x 5.64444cm

parts:
  LCD1 = LCD screen
  LVL1 = Logic Level Converter
  LED1 = LED - 5mm [color="Red (633nm)" package="5 mm [THT]"]
  R1 = Trimmer Potentiometer [maximum_resistance=10kΩ package=THT]
  Q1 = NPN-Transistor [package="TO92 [THT]"]
  LVL2 = Logic Level Converter
  WeMos_D1_Mini1 = WeMos D1 Mini

nets:
  VSS: LCD1.VSS, LCD1.R/W, LVL1.GND, LED1.cathode, R1.leg1, Q1.C, WeMos_D1_Mini1.G
  VDD: LCD1.VDD, LCD1.LED+, LVL1.HV, R1.leg2, LVL2.HV, WeMos_D1_Mini1.5V
  N1: LCD1.V0, R1.wiper
  N2: LCD1.RS, LVL2.RX_HV
  N3: LCD1.E, LVL2.TX_HV
  N4: LCD1.DB4, LVL1.TX2_HV
  N5: LCD1.DB5, LVL1.RX2_HV
  N6: LCD1.DB6, LVL1.RX_HV
  N7: LCD1.DB7, LVL1.TX_HV
  N8: LCD1.LED-, Q1.E
  N9: LVL1.TX2_LV, WeMos_D1_Mini1.D5
  N10: LVL1.RX2_LV, WeMos_D1_Mini1.D6
  N11: LVL1.LV, LVL2.LV, WeMos_D1_Mini1.3V3
  N12: LVL1.RX_LV, WeMos_D1_Mini1.D7
  N13: LVL1.TX_LV, WeMos_D1_Mini1.D8
  N14: LED1.anode, WeMos_D1_Mini1.D4
  N15: Q1.B, LVL2.TX2_HV
  N16: LVL2.TX2_LV, WeMos_D1_Mini1.D3
  N17: LVL2.RX_LV, WeMos_D1_Mini1.D2
  N18: LVL2.TX_LV, WeMos_D1_Mini1.D1
